// Logisim project Magnitude_comparator.circ as structural Verilog: 1 circuit, main circuit main
module main (
);

  wire and_1_out, and_2_out, and_3_out, and_4_out, and_5_out, and_6_out, and_7_out, and_8_out, and_9_out,
       and_10_out, buffer_1_out, buffer_2_out, buffer_3_out, buffer_4_out, buffer_5_out, buffer_6_out,
       buffer_7_out, buffer_8_out, buffer_9_out, buffer_10_out, buffer_11_out, buffer_12_out, buffer_13_out,
       buffer_14_out, buffer_15_out, buffer_16_out, buffer_17_out, dipswitch_1_p1, dipswitch_1_p2,
       dipswitch_1_p3, dipswitch_1_p4, dipswitch_2_p1, dipswitch_2_p2, dipswitch_2_p3, dipswitch_2_p4,
       nor_1_out, nor_2_out, nor_3_out, nor_4_out, not_1_out, not_2_out, not_3_out, not_4_out, not_5_out,
       not_6_out, not_7_out, not_8_out, or_1_out, or_2_out, or_3_out, or_4_out, or_5_out, or_6_out;

  // DipSwitch dipswitch_1: pin names not known; wires that end beside it: dipswitch_1_p1, dipswitch_1_p2, dipswitch_1_p3, dipswitch_1_p4
  // DipSwitch dipswitch_2: pin names not known; wires that end beside it: dipswitch_2_p1, dipswitch_2_p2, dipswitch_2_p3, dipswitch_2_p4
  buf buffer_1 (buffer_1_out, dipswitch_1_p1);
  buf buffer_2 (buffer_2_out, dipswitch_2_p1);
  buf buffer_3 (buffer_3_out, dipswitch_1_p2);
  buf buffer_4 (buffer_4_out, dipswitch_2_p2);
  buf buffer_5 (buffer_5_out, dipswitch_1_p3);
  buf buffer_6 (buffer_6_out, dipswitch_2_p3);
  buf buffer_7 (buffer_7_out, dipswitch_1_p4);
  buf buffer_8 (buffer_8_out, dipswitch_2_p4);
  not not_1 (not_1_out, buffer_1_out);
  not not_2 (not_2_out, buffer_2_out);
  buf buffer_9 (buffer_9_out, and_1_out);
  and and_1 (and_1_out, buffer_10_out, nor_1_out);
  not not_3 (not_3_out, buffer_3_out);
  not not_4 (not_4_out, buffer_4_out);
  buf buffer_10 (buffer_10_out, and_2_out);
  and and_2 (and_2_out, buffer_11_out, nor_2_out);
  not not_5 (not_5_out, buffer_5_out);
  not not_6 (not_6_out, buffer_6_out);
  buf buffer_11 (buffer_11_out, nor_3_out);
  not not_7 (not_7_out, buffer_7_out);
  not not_8 (not_8_out, buffer_8_out);
  and and_3 (and_3_out, not_1_out, buffer_9_out, buffer_2_out);
  and and_4 (and_4_out, buffer_1_out, buffer_9_out, not_2_out);
  and and_5 (and_5_out, not_3_out, buffer_10_out, buffer_4_out);
  and and_6 (and_6_out, buffer_3_out, buffer_10_out, not_4_out);
  and and_7 (and_7_out, not_5_out, buffer_11_out, buffer_6_out);
  and and_8 (and_8_out, buffer_5_out, buffer_11_out, not_6_out);
  and and_9 (and_9_out, not_7_out, buffer_8_out);
  and and_10 (and_10_out, buffer_7_out, not_8_out);
  buf buffer_12 (buffer_12_out, and_4_out);
  nor nor_1 (nor_1_out, and_5_out, and_6_out);
  buf buffer_13 (buffer_13_out, or_2_out);
  nor nor_2 (nor_2_out, and_7_out, and_8_out);
  buf buffer_14 (buffer_14_out, or_4_out);
  nor nor_3 (nor_3_out, and_9_out, and_10_out);
  buf buffer_15 (buffer_15_out, and_3_out);
  or or_1 (or_1_out, buffer_15_out, and_5_out);
  or or_2 (or_2_out, buffer_12_out, and_6_out);
  buf buffer_16 (buffer_16_out, or_1_out);
  or or_3 (or_3_out, buffer_16_out, and_7_out);
  or or_4 (or_4_out, buffer_13_out, and_8_out);
  buf buffer_17 (buffer_17_out, or_3_out);
  or or_5 (or_5_out, buffer_17_out, and_9_out);
  or or_6 (or_6_out, buffer_14_out, and_10_out);
  LED led_1 (.in(or_5_out));
  nor nor_4 (nor_4_out, or_5_out, or_6_out);
  LED led_2 (.in(nor_4_out));
  LED led_3 (.in(or_6_out));

  // Notes on the sheet:
  //   A
  //   B
  //   A
  //   B
  //   A
  //   B
  //   A
  //   B
  //   Supress
  //   Supress
  //   Supress
  //   A > B
  //   A > B
  //   A > B
  //   A < B
  //   A < B
  //   A < B
  //   A < B
  //   A == B
  //   A > B
endmodule
