// Logisim project binary_counter.circ as structural Verilog: 1 circuit, main circuit main
module main (
);

  wire and_1_out, and_2_out, and_3_out, and_4_out, and_5_out, and_6_out, and_7_out, and_8_out, and_9_out,
       and_10_out, and_11_out, and_12_out, and_13_out, and_14_out, and_15_out, dipswitch_1_p1,
       dipswitch_1_p2, dipswitch_1_p3, nand_1_out, nand_2_out, nand_3_out, nand_4_out, nand_5_out,
       nand_6_out, nand_7_out, nand_8_out, nand_9_out, nand_10_out, nand_11_out, nand_12_out, nand_13_out,
       nand_14_out, nand_15_out, nand_16_out, nand_17_out, nand_18_out, nand_19_out, nand_20_out,
       nand_21_out, nand_22_out, nand_23_out, nand_24_out, nor_1_out;

  // DipSwitch #(.number(3)) dipswitch_1: pin names not known; wires that end beside it: dipswitch_1_p1, dipswitch_1_p2, dipswitch_1_p3
  nand nand_1 (nand_1_out, nand_2_out, nand_9_out);
  nand nand_2 (nand_2_out, nand_18_out, dipswitch_1_p3, nand_10_out);
  nand nand_3 (nand_3_out, nand_4_out, nand_11_out);
  nand nand_4 (nand_4_out, nand_20_out, dipswitch_1_p3, nand_12_out);
  nand nand_5 (nand_5_out, nand_6_out, nand_13_out);
  nand nand_6 (nand_6_out, nand_22_out, dipswitch_1_p3, nand_14_out);
  nand nand_7 (nand_7_out, nand_8_out, nand_15_out);
  nand nand_8 (nand_8_out, nand_24_out, dipswitch_1_p3, nand_16_out);
  nand nand_9 (nand_9_out, nand_1_out, dipswitch_1_p3, dipswitch_1_p2);
  nand nand_10 (nand_10_out, nand_9_out, dipswitch_1_p2, nand_2_out);
  nand nand_11 (nand_11_out, nand_3_out, dipswitch_1_p3, nand_18_out);
  nand nand_12 (nand_12_out, nand_11_out, nand_18_out, nand_4_out);
  nand nand_13 (nand_13_out, nand_5_out, dipswitch_1_p3, nand_20_out);
  nand nand_14 (nand_14_out, nand_13_out, nand_20_out, nand_6_out);
  nand nand_15 (nand_15_out, nand_7_out, dipswitch_1_p3, nand_22_out);
  nand nand_16 (nand_16_out, nand_15_out, nand_22_out, nand_8_out);
  nand nand_17 (nand_17_out, nand_9_out, nand_18_out);
  nand nand_18 (nand_18_out, nand_17_out, dipswitch_1_p1, nand_10_out);
  nand nand_19 (nand_19_out, nand_11_out, nand_20_out);
  nand nand_20 (nand_20_out, nand_19_out, dipswitch_1_p1, nand_12_out);
  nand nand_21 (nand_21_out, nand_13_out, nand_22_out);
  nand nand_22 (nand_22_out, nand_21_out, dipswitch_1_p1, nand_14_out);
  nand nand_23 (nand_23_out, nand_15_out, nand_24_out);
  nand nand_24 (nand_24_out, nand_23_out, dipswitch_1_p1, nand_16_out);
  LED led_1 (.in(nand_17_out));
  LED led_2 (.in(nand_19_out));
  LED led_3 (.in(nand_21_out));
  LED led_4 (.in(nand_23_out));
  LED led_5 (.in(and_1_out));
  LED led_6 (.in(nor_1_out));
  nor nor_1 (nor_1_out, nand_17_out, nand_19_out, nand_21_out, nand_23_out);
  and and_1 (and_1_out, nand_17_out, nand_20_out, nand_22_out, nand_24_out);
  LED led_7 (.in(and_2_out));
  and and_2 (and_2_out, nand_18_out, nand_19_out, nand_22_out, nand_24_out);
  LED led_8 (.in(and_3_out));
  and and_3 (and_3_out, nand_17_out, nand_19_out, nand_22_out, nand_24_out);
  LED led_9 (.in(and_4_out));
  LED led_10 (.in(and_5_out));
  and and_4 (and_4_out, nand_18_out, nand_20_out, nand_21_out, nand_24_out);
  and and_5 (and_5_out, nand_17_out, nand_21_out, nand_20_out, nand_24_out);
  LED led_11 (.in(and_6_out));
  and and_6 (and_6_out, nand_18_out, nand_19_out, nand_21_out, nand_24_out);
  LED led_12 (.in(and_7_out));
  and and_7 (and_7_out, nand_17_out, nand_19_out, nand_21_out, nand_24_out);
  LED led_13 (.in(and_8_out));
  LED led_14 (.in(and_9_out));
  and and_8 (and_8_out, nand_18_out, nand_20_out, nand_22_out, nand_23_out);
  and and_9 (and_9_out, nand_17_out, nand_20_out, nand_22_out, nand_23_out);
  LED led_15 (.in(and_10_out));
  and and_10 (and_10_out, nand_18_out, nand_19_out, nand_22_out, nand_23_out);
  LED led_16 (.in(and_11_out));
  and and_11 (and_11_out, nand_17_out, nand_19_out, nand_22_out, nand_23_out);
  LED led_17 (.in(and_12_out));
  LED led_18 (.in(and_13_out));
  and and_12 (and_12_out, nand_18_out, nand_20_out, nand_21_out, nand_23_out);
  and and_13 (and_13_out, nand_17_out, nand_20_out, nand_21_out, nand_23_out);
  LED led_19 (.in(and_14_out));
  and and_14 (and_14_out, nand_18_out, nand_19_out, nand_21_out, nand_23_out);
  LED led_20 (.in(and_15_out));
  and and_15 (and_15_out, nand_17_out, nand_19_out, nand_21_out, nand_23_out);
endmodule
