// Logisim project d_latch.circ as structural Verilog: 1 circuit, main circuit main
module main (
);

  wire dipswitch_1_p1, dipswitch_1_p2, dipswitch_1_p3, nand_1_out, nand_2_out, nand_3_out, nand_4_out,
       nand_5_out, nand_6_out;

  // DipSwitch #(.number(3)) dipswitch_1: pin names not known; wires that end beside it: dipswitch_1_p1, dipswitch_1_p2, dipswitch_1_p3
  nand nand_1 (nand_1_out, nand_4_out, nand_2_out);
  nand nand_2 (nand_2_out, nand_1_out, dipswitch_1_p1);
  nand nand_3 (nand_3_out, nand_2_out, dipswitch_1_p1, nand_4_out);
  nand nand_4 (nand_4_out, nand_3_out, dipswitch_1_p2);
  LED led_1 (.in(nand_5_out));
  nand nand_5 (nand_5_out, nand_2_out, nand_6_out);
  nand nand_6 (nand_6_out, nand_5_out, dipswitch_1_p3, nand_3_out);
endmodule
