// Logisim project full_adder_substractor.circ as structural Verilog: 1 circuit, main circuit main
module main (
);

  wire and_1_out, and_2_out, and_3_out, and_4_out, and_5_out, and_6_out, and_7_out, and_8_out, buffer_1_out,
       buffer_2_out, buffer_3_out, buffer_4_out, buffer_5_out, buffer_6_out, buffer_7_out, buffer_8_out,
       buffer_9_out, buffer_10_out, buffer_11_out, buffer_12_out, buffer_13_out, buffer_14_out,
       dipswitch_1_p1, dipswitch_2_p1, dipswitch_2_p2, dipswitch_2_p3, dipswitch_3_p1, dipswitch_3_p2,
       dipswitch_3_p3, dipswitch_3_p4, dipswitch_3_p5, or_1_out, or_2_out, or_3_out, or_4_out, xor_1_out,
       xor_2_out, xor_3_out, xor_4_out, xor_5_out, xor_6_out, xor_7_out, xor_8_out, xor_9_out, xor_10_out,
       xor_11_out, xor_12_out;

  // DipSwitch #(.number(2)) dipswitch_1: pin names not known; wires that end beside it: dipswitch_1_p1
  // DipSwitch #(.number(4)) dipswitch_2: pin names not known; wires that end beside it: dipswitch_2_p1, dipswitch_2_p2, dipswitch_2_p3
  // DipSwitch #(.number(4)) dipswitch_3: pin names not known; wires that end beside it: dipswitch_3_p1, dipswitch_3_p2, dipswitch_3_p3, dipswitch_3_p4, dipswitch_3_p5
  buf buffer_1 (buffer_1_out, dipswitch_1_p1);
  buf buffer_2 (buffer_2_out, dipswitch_2_p1);
  buf buffer_3 (buffer_3_out, dipswitch_3_p2);
  buf buffer_4 (buffer_4_out, dipswitch_2_p2);
  buf buffer_5 (buffer_5_out, dipswitch_3_p3);
  buf buffer_6 (buffer_6_out, dipswitch_2_p3);
  buf buffer_7 (buffer_7_out, dipswitch_3_p4);
  buf buffer_8 (buffer_8_out, dipswitch_3_p1);
  buf buffer_9 (buffer_9_out, dipswitch_3_p5);
  xor xor_1 (xor_1_out, buffer_1_out, buffer_3_out);
  xor xor_2 (xor_2_out, buffer_1_out, buffer_5_out);
  xor xor_3 (xor_3_out, buffer_1_out, buffer_7_out);
  xor xor_4 (xor_4_out, buffer_1_out, buffer_9_out);
  xor xor_5 (xor_5_out, buffer_2_out, xor_1_out);
  and and_1 (and_1_out, buffer_2_out, xor_1_out);
  xor xor_6 (xor_6_out, buffer_4_out, xor_2_out);
  and and_2 (and_2_out, buffer_4_out, xor_2_out);
  xor xor_7 (xor_7_out, buffer_6_out, xor_3_out);
  and and_3 (and_3_out, buffer_6_out, xor_3_out);
  xor xor_8 (xor_8_out, buffer_8_out, xor_4_out);
  and and_4 (and_4_out, buffer_8_out, xor_4_out);
  xor xor_9 (xor_9_out, buffer_1_out, xor_5_out);
  and and_5 (and_5_out, buffer_1_out, xor_5_out);
  xor xor_10 (xor_10_out, or_1_out, xor_6_out);
  and and_6 (and_6_out, or_1_out, xor_6_out);
  xor xor_11 (xor_11_out, or_2_out, xor_7_out);
  and and_7 (and_7_out, or_2_out, xor_7_out);
  xor xor_12 (xor_12_out, or_3_out, xor_8_out);
  and and_8 (and_8_out, or_3_out, xor_8_out);
  buf buffer_10 (buffer_10_out, xor_9_out);
  LED led_1 (.in(buffer_10_out));
  or or_1 (or_1_out, and_5_out, and_1_out);
  buf buffer_11 (buffer_11_out, xor_10_out);
  LED led_2 (.in(buffer_11_out));
  or or_2 (or_2_out, and_6_out, and_2_out);
  buf buffer_12 (buffer_12_out, xor_11_out);
  LED led_3 (.in(buffer_12_out));
  or or_3 (or_3_out, and_7_out, and_3_out);
  buf buffer_13 (buffer_13_out, xor_12_out);
  LED led_4 (.in(buffer_13_out));
  or or_4 (or_4_out, and_8_out, and_4_out);
  buf buffer_14 (buffer_14_out, or_4_out);
  LED led_5 (.in(buffer_14_out));
endmodule
