// Logisim project register.circ as structural Verilog: 1 circuit, main circuit main
module main (
);

  wire dipswitch_1_p1, dipswitch_1_p2, dipswitch_2_p1, dipswitch_2_p2, dipswitch_2_p3, dipswitch_2_p4,
       nand_1_out, nand_2_out, nand_3_out, nand_4_out, nand_5_out, nand_6_out, nand_7_out, nand_8_out,
       nand_9_out, nand_10_out, nand_11_out, nand_12_out, nand_13_out, nand_14_out, nand_15_out, nand_16_out,
       nand_17_out, nand_18_out, nand_19_out, nand_20_out, nand_21_out, nand_22_out, nand_23_out, nand_24_out;

  // DipSwitch #(.number(2)) dipswitch_1: pin names not known; wires that end beside it: dipswitch_1_p1, dipswitch_1_p2
  // DipSwitch #(.number(4)) dipswitch_2: pin names not known; wires that end beside it: dipswitch_2_p1, dipswitch_2_p2, dipswitch_2_p3, dipswitch_2_p4
  nand nand_1 (nand_1_out, nand_2_out, nand_9_out);
  nand nand_2 (nand_2_out, dipswitch_2_p1, nand_10_out);
  nand nand_3 (nand_3_out, nand_4_out, nand_11_out);
  nand nand_4 (nand_4_out, dipswitch_2_p2, nand_12_out);
  nand nand_5 (nand_5_out, nand_6_out, nand_13_out);
  nand nand_6 (nand_6_out, dipswitch_2_p3, nand_14_out);
  nand nand_7 (nand_7_out, nand_8_out, nand_15_out);
  nand nand_8 (nand_8_out, dipswitch_2_p4, nand_16_out);
  nand nand_9 (nand_9_out, nand_1_out, dipswitch_1_p2);
  nand nand_10 (nand_10_out, nand_9_out, dipswitch_1_p2, nand_2_out);
  nand nand_11 (nand_11_out, nand_3_out, dipswitch_1_p2);
  nand nand_12 (nand_12_out, nand_11_out, dipswitch_1_p2, nand_4_out);
  nand nand_13 (nand_13_out, nand_5_out, dipswitch_1_p2);
  nand nand_14 (nand_14_out, nand_13_out, dipswitch_1_p2, nand_6_out);
  nand nand_15 (nand_15_out, nand_7_out, dipswitch_1_p2);
  nand nand_16 (nand_16_out, nand_15_out, dipswitch_1_p2, nand_8_out);
  nand nand_17 (nand_17_out, nand_9_out, nand_18_out);
  nand nand_18 (nand_18_out, nand_17_out, dipswitch_1_p1, nand_10_out);
  nand nand_19 (nand_19_out, nand_11_out, nand_20_out);
  nand nand_20 (nand_20_out, nand_19_out, dipswitch_1_p1, nand_12_out);
  nand nand_21 (nand_21_out, nand_13_out, nand_22_out);
  nand nand_22 (nand_22_out, nand_21_out, dipswitch_1_p1, nand_14_out);
  nand nand_23 (nand_23_out, nand_15_out, nand_24_out);
  nand nand_24 (nand_24_out, nand_23_out, dipswitch_1_p1, nand_16_out);
  LED led_1 (.in(nand_17_out));
  LED led_2 (.in(nand_19_out));
  LED led_3 (.in(nand_21_out));
  LED led_4 (.in(nand_23_out));
endmodule
